// Logisim project 74LS74.circ as structural Verilog: 1 circuit, main circuit 74LS74
module _74LS74 (
  input  _1CLK,
  input  _2CLK,
  input  _1D,
  input  _2D,
  input  _1_PRE,
  input  _2_PRE,
  input  _1_CLR,
  input  _2_CLR,
  output _1Q,
  output _2Q,
  output _1_Q,
  output _2_Q
);

  wire not_1_out, not_2_out, not_3_out, not_4_out;

  not not_1 (not_1_out, _1_PRE);
  not not_2 (not_2_out, _1_CLR);
  D_Flip_Flop d_ff_1 (.clk(_1CLK), .D(_1D), .Q(_1Q), .Qn(_1_Q), .preset(not_1_out), .reset(not_2_out));  // open: en
  not not_3 (not_3_out, _2_PRE);
  not not_4 (not_4_out, _2_CLR);
  D_Flip_Flop d_ff_2 (.clk(_2CLK), .D(_2D), .Q(_2Q), .Qn(_2_Q), .preset(not_3_out), .reset(not_4_out));  // open: en

  // Notes on the sheet:
  //   74LS74
endmodule
