// Logisim project 74LS92.circ as structural Verilog: 1 circuit, main circuit 74LS92
module _74LS92 (
  input  in_1,
  input  in_2,
  input  in_3,
  input  in_4,
  output out_5,
  output out_6,
  output out_7,
  output out_8
);

  wire j_k_ff_3_qn, nand_1_out, not_1_out, not_2_out, not_3_out, not_4_out, not_5_out;

  nand nand_1 (nand_1_out, in_3, in_4);
  not not_1 (not_1_out, in_1);
  not not_2 (not_2_out, in_2);
  not not_3 (not_3_out, in_2);
  not not_4 (not_4_out, out_7);
  not not_5 (not_5_out, nand_1_out);
  J_K_Flip_Flop j_k_ff_1 (.J(1'b1), .clk(not_1_out), .K(1'b1), .Q(out_5), .reset(not_5_out));  // open: Qn, preset, en
  J_K_Flip_Flop j_k_ff_2 (
    .J(j_k_ff_3_qn), .clk(not_2_out), .K(1'b1), .Q(out_6), .reset(not_5_out));  // open: Qn, preset, en
  J_K_Flip_Flop j_k_ff_3 (
    .J(out_6), .clk(not_3_out), .K(1'b1), .Q(out_7), .Qn(j_k_ff_3_qn), .reset(not_5_out));  // open: preset, en
  J_K_Flip_Flop j_k_ff_4 (.J(1'b1), .clk(not_4_out), .K(1'b1), .Q(out_8), .reset(not_5_out));  // open: Qn, preset, en

  // Notes on the sheet:
  //   74LS92
endmodule
