// Logisim project 74LS93.circ as structural Verilog: 1 circuit, main circuit 74LS93
module _74LS93 (
  input  CKA,
  input  CKB,
  input  R0_1,
  input  R0_2,
  output QA,
  output QB,
  output QC,
  output QD
);

  wire nand_1_out, not_1_out, not_2_out, not_3_out, not_4_out, not_5_out;

  not not_1 (not_1_out, CKA);
  not not_2 (not_2_out, CKB);
  not not_3 (not_3_out, QB);
  not not_4 (not_4_out, QC);
  not not_5 (not_5_out, nand_1_out);
  nand nand_1 (nand_1_out, R0_1, R0_2);
  J_K_Flip_Flop j_k_ff_1 (.J(1'b1), .clk(not_1_out), .K(1'b1), .Q(QA), .reset(not_5_out));  // open: Qn, preset, en
  J_K_Flip_Flop j_k_ff_2 (.J(1'b1), .clk(not_2_out), .K(1'b1), .Q(QB), .reset(not_5_out));  // open: Qn, preset, en
  J_K_Flip_Flop j_k_ff_3 (.J(1'b1), .clk(not_3_out), .K(1'b1), .Q(QC), .reset(not_5_out));  // open: Qn, preset, en
  J_K_Flip_Flop j_k_ff_4 (.J(1'b1), .clk(not_4_out), .K(1'b1), .Q(QD), .reset(not_5_out));  // open: Qn, preset, en

  // Notes on the sheet:
  //   74LS93
endmodule
