// Logisim project OSI440B-Counter.circ as structural Verilog: 1 circuit, main circuit main
module main (
);

  wire clock_1_out, n74ls163_2_rco, n74ls163_3_rco, n74ls163_4_rco, pull_resistor_1_node;
  wire [3:0] n74ls163_1_qa, n74ls163_2_qa, n74ls163_3_qa, n74ls163_4_qa;

  Pull_Resistor #(.pull(1)) pull_resistor_1 (.node(pull_resistor_1_node));
  Hex_Digit_Display hex_digit_display_1 (.value(n74ls163_1_qa));  // open: dp
  _74LS163 u_74ls163_1 (
    .nLOAD(pull_resistor_1_node), .CLK(clock_1_out), .nCLR(pull_resistor_1_node), .ENP(n74ls163_4_rco),
    .ENT(n74ls163_2_rco), .QA(n74ls163_1_qa[0]), .QB(n74ls163_1_qa[1]), .QC(n74ls163_1_qa[2]),
    .QD(n74ls163_1_qa[3]));  // open: DATA_A, DATA_B, DATA_C, DATA_D, RCO
  Hex_Digit_Display hex_digit_display_2 (.value(n74ls163_2_qa));  // open: dp
  Clock clock_1 (.out(clock_1_out));
  _74LS163 u_74ls163_2 (
    .nLOAD(pull_resistor_1_node), .CLK(clock_1_out), .nCLR(pull_resistor_1_node), .ENP(n74ls163_4_rco),
    .ENT(n74ls163_3_rco), .QA(n74ls163_2_qa[0]), .QB(n74ls163_2_qa[1]), .QC(n74ls163_2_qa[2]),
    .QD(n74ls163_2_qa[3]), .RCO(n74ls163_2_rco));  // open: DATA_A, DATA_B, DATA_C, DATA_D
  Hex_Digit_Display hex_digit_display_3 (.value(n74ls163_3_qa));  // open: dp
  _74LS163 u_74ls163_3 (
    .nLOAD(pull_resistor_1_node), .CLK(clock_1_out), .nCLR(pull_resistor_1_node), .ENP(n74ls163_4_rco),
    .ENT(n74ls163_4_rco), .QA(n74ls163_3_qa[0]), .QB(n74ls163_3_qa[1]), .QC(n74ls163_3_qa[2]),
    .QD(n74ls163_3_qa[3]), .RCO(n74ls163_3_rco));  // open: DATA_A, DATA_B, DATA_C, DATA_D
  Hex_Digit_Display hex_digit_display_4 (.value(n74ls163_4_qa));  // open: dp
  _74LS163 u_74ls163_4 (
    .nLOAD(pull_resistor_1_node), .CLK(clock_1_out), .nCLR(pull_resistor_1_node), .ENP(pull_resistor_1_node),
    .ENT(pull_resistor_1_node), .QA(n74ls163_4_qa[0]), .QB(n74ls163_4_qa[1]), .QC(n74ls163_4_qa[2]),
    .QD(n74ls163_4_qa[3]), .RCO(n74ls163_4_rco));  // open: DATA_A, DATA_B, DATA_C, DATA_D

  // Notes on the sheet:
  //   OSI 440B 16-bit counter
endmodule
