// Logisim project OSI540B-Counters.circ as structural Verilog: 1 circuit, main circuit main
module main (
  input  _32,
  output DOT_SHAPE
);

  wire A0, A1, A2, A3, A4, A5, A6, A7, A8, A9, C0, C1, C2, COL_CLOCK, END_BLANK, n74ls74_1__1_q,
       n74ls74_1__2_q, n74ls74_1__2q, n74ls92_1_out_5, n74ls92_1_out_7, n74ls163_1_rco, n74ls163_2_rco,
       n74ls163_3_qd, n74ls163_3_rco, n74ls163_4_qa, n74ls163_4_qb, n74ls163_4_qc, n74ls163_5_qd,
       n74ls163_5_rco, n74ls163_6_qa, n74ls163_6_qb, n74ls163_6_qc, n74ls163_6_qd, n74ls163_6_rco,
       n74ls163_7_qa, n74ls163_7_qb, nand_1_out, nand_2_out, nand_3_out, nand_4_out, nand_5_out, nCE0, nCE1,
       nCEA, nCEB, nCOL_CLEAR, nDOT_INHIBIT, nEND_BLANK, nHS, nR7, nVAS, PHI0, pull_resistor_1_node,
       pull_resistor_3_node, R0, R1, R2, R7, S1, S4, S5, S6, S7, undriven, VA0, VA1, VA2, VA3, VA4, VA5, VA6,
       VA7, VA8, VA9, XTAL_out;

  Hex_Digit_Display hex_digit_display_1 (.value({S7, S6, S5, S4}));  // open: dp
  Hex_Digit_Display hex_digit_display_2 (.value({1'b0, R2, R1, R0}));  // open: dp
  LED led_1 (.in(S1));
  Clock XTAL (.out(XTAL_out));
  nand nand_1 (nand_1_out, XTAL_out, XTAL_out);
  Pull_Resistor #(.pull(1)) pull_resistor_1 (.node(pull_resistor_1_node));
  nand nand_2 (nand_2_out, pull_resistor_1_node, S6);
  nand nand_3 (nand_3_out, pull_resistor_1_node, S7);
  _74LS163 u_74ls163_1 (
    .nLOAD(1'b1), .DATA_A(1'b0), .DATA_B(1'b0), .CLK(n74ls92_1_out_7), .DATA_C(1'b0), .DATA_D(1'b0),
    .nCLR(1'b1), .ENP(1'b1), .ENT(1'b1), .QB(S1), .RCO(n74ls163_1_rco));  // open: QA, QC, QD
  _74LS163 u_74ls163_2 (
    .nLOAD(1'b1), .DATA_A(1'b0), .DATA_B(1'b0), .CLK(n74ls92_1_out_7), .DATA_C(1'b0), .DATA_D(1'b0),
    .nCLR(1'b1), .ENP(n74ls163_1_rco), .ENT(n74ls163_1_rco), .QA(S4), .QB(S5), .QC(S6), .QD(S7),
    .RCO(n74ls163_2_rco));
  _74LS163 u_74ls163_3 (
    .nLOAD(1'b1), .DATA_A(1'b0), .DATA_B(1'b0), .CLK(n74ls92_1_out_7), .DATA_C(1'b0), .DATA_D(1'b0),
    .nCLR(1'b1), .ENP(n74ls163_1_rco), .ENT(n74ls163_2_rco), .QA(R0), .QB(R1), .QC(R2), .QD(n74ls163_3_qd),
    .RCO(n74ls163_3_rco));
  _74LS163 u_74ls163_4 (
    .nLOAD(1'b1), .DATA_A(1'b0), .DATA_B(1'b0), .CLK(n74ls92_1_out_7), .DATA_C(1'b0), .DATA_D(1'b0),
    .nCLR(1'b1), .ENP(n74ls163_1_rco), .ENT(n74ls163_3_rco), .QA(n74ls163_4_qa), .QB(n74ls163_4_qb),
    .QC(n74ls163_4_qc), .QD(R7));  // open: RCO
  _74LS92 u_74ls92_1 (
    .in_1(nand_1_out), .in_2(nand_1_out), .in_3(1'b0), .in_4(1'b0), .out_5(n74ls92_1_out_5),
    .out_7(n74ls92_1_out_7));  // open: out_6, out_8
  nand nand_4 (nand_4_out, S4, S5, nand_2_out, nand_3_out);
  not not_1 (nEND_BLANK, END_BLANK);
  _74LS163 u_74ls163_5 (
    .nLOAD(1'b1), .DATA_A(1'b0), .DATA_B(1'b0), .CLK(COL_CLOCK), .DATA_C(1'b0), .DATA_D(1'b0),
    .nCLR(nCOL_CLEAR), .ENP(1'b1), .ENT(1'b1), .QA(C0), .QB(C1), .QC(C2), .QD(n74ls163_5_qd),
    .RCO(n74ls163_5_rco));
  _74LS163 u_74ls163_6 (
    .nLOAD(1'b1), .DATA_A(1'b0), .DATA_B(1'b0), .CLK(COL_CLOCK), .DATA_C(1'b0), .DATA_D(1'b0),
    .nCLR(nCOL_CLEAR), .ENP(n74ls163_5_rco), .ENT(n74ls163_5_rco), .QA(n74ls163_6_qa), .QB(n74ls163_6_qb),
    .QC(n74ls163_6_qc), .QD(n74ls163_6_qd), .RCO(n74ls163_6_rco));
  _74LS163 u_74ls163_7 (
    .nLOAD(1'b1), .DATA_A(1'b0), .DATA_B(1'b0), .CLK(COL_CLOCK), .DATA_C(1'b0), .DATA_D(1'b0),
    .nCLR(nCOL_CLEAR), .ENP(n74ls163_5_rco), .ENT(n74ls163_6_rco), .QA(n74ls163_7_qa), .QB(n74ls163_7_qb));  // open: QC, QD, RCO
  _74LS74 u_74ls74_1 (
    ._1CLK(1'b0), ._2CLK(1'b0), ._1D(1'b0), ._2D(1'b0), ._1_PRE(n74ls74_1__2_q), ._2_PRE(nand_4_out),
    ._1_CLR(nHS), ._2_CLR(nEND_BLANK), ._2Q(n74ls74_1__2q), ._1_Q(n74ls74_1__1_q), ._2_Q(n74ls74_1__2_q));  // open: _1Q
  not not_2 (nR7, R7);
  _74LS157 u_74ls157_1 (
    ._1A(n74ls92_1_out_5), ._1B(nand_1_out), ._2A(n74ls163_7_qa), ._2B(n74ls163_7_qb), .STROBE_nG(1'b0),
    .SELECT_A_B(_32), ._1Y(COL_CLOCK), ._2Y(END_BLANK));  // open: _3A, _3B, _4A, _4B, _3Y, _4Y
  nand nand_5 (nand_5_out, n74ls74_1__2q, undriven);
  not not_3 (nDOT_INHIBIT, nand_5_out);
  nand nand_6 (nCOL_CLEAR, n74ls74_1__1_q, n74ls74_1__1_q);
  _74LS157 u_74ls157_2 (
    ._1A(A1), ._1B(n74ls163_6_qa), ._2A(A3), ._2B(n74ls163_6_qc), ._3A(A0), ._3B(n74ls163_5_qd), ._4A(A2),
    ._4B(n74ls163_6_qb), .STROBE_nG(1'b0), .SELECT_A_B(nVAS), ._1Y(VA0), ._2Y(VA1), ._3Y(VA2), ._4Y(VA3));
  _74LS157 u_74ls157_3 (
    ._1A(A7), ._1B(n74ls163_4_qa), ._2A(A4), ._2B(n74ls163_6_qd), ._3A(A5), ._3B(n74ls163_7_qa), ._4A(A6),
    ._4B(n74ls163_3_qd), .STROBE_nG(1'b0), .SELECT_A_B(nVAS), ._1Y(VA4), ._2Y(VA5), ._3Y(VA6), ._4Y(VA7));
  _74LS157 u_74ls157_4 (
    ._1A(A8), ._1B(n74ls163_4_qb), ._2A(A9), ._2B(n74ls163_4_qc), ._3A(nCE0), ._3B(R7), ._4A(nCE1),
    ._4B(nR7), .STROBE_nG(1'b0), .SELECT_A_B(nVAS), ._1Y(VA8), ._2Y(VA9), ._3Y(nCEA), ._4Y(nCEB));
  Pull_Resistor #(.pull(1)) pull_resistor_2 (.node(nVAS));
  or or_1 (DOT_SHAPE, ~nand_1_out, ~nand_1_out);  // OR_Gate
  Pull_Resistor #(.pull(1)) pull_resistor_3 (.node(pull_resistor_3_node));
  nand nand_7 (PHI0, S1, pull_resistor_3_node, pull_resistor_3_node);

  // Notes on the sheet:
  //   OSI 540B
  //   Counters
  //   CLOCK/3
  //   A
  //   A
  //   A
  //   74123, B and /CLR pulled high
  //   Cext/R = 1000pF and 16K
  //   Tw = 0.28*16*1000*(1+0.7/16)
  //   Tw = 4676 ns = 4.676 us
  //   74123, B and /CLR pulled high
  //   Cext/R = 1000pF and 10K
  //   Tw = 0.28*10*1000*(1+0.7/10)
  //   Tw = 2996 ns = 2.996 us
  //   74123, B and /CLR pulled high
  //   Cext/R = 100000pF and 10K
  //   Tw = 0.28*10*100000*(1+0.7/10)
  //   Tw = 299600 ns = 299.6 us
  //   CLOCK
  //   /6
  //   /12
  //   /24
  //   etc..
  //   /768
  //   CLOCK/196608
  //   CLOCK/2
  //   CLOCK/3
  //   (33/67 duty)
  //   CLOCK
  //   ___
  //   _
  //   Q =
  //   HS
  //   _
  //   ___
  //   Q =
  //   VS
  //   CLOCK/2
  //   Black/White
  //   XTAL CLOCK
  //   11.79MHz
  //   Vert. Freq. = 11790000 / 196608 = 59.967041 Hz
  //   Color
  //   XTAL CLOCK
  //   12.08MHz
  //   CLOCK
  //   Hor. Freq. = 11790000 / 768 = 15351.563 Hz
  //   Hor. Freq. = 12080000 / 768 = 15729.167 Hz
  //   Vert. Freq. = 12080000 / 196608 = 61.442057 Hz
  //   debug
  //   CPU CLOCK
  //   FROM VIDEO CIRCUIT
  //   XTAL / 12
endmodule
