// Logisim project OSI600.circ as structural Verilog: 1 circuit, main circuit main
module main (
);

  wire CLOCK_out, n74ls92_1_out_6, n74ls93_1_qa, n74ls93_1_qb, n74ls93_1_qc, n74ls93_1_qd;

  Clock CLOCK (.out(CLOCK_out));
  _74LS93 u_74ls93_1 (
    .CKA(n74ls93_1_qc), .CKB(CLOCK_out), .R0_1(1'b0), .R0_2(1'b0), .QA(n74ls93_1_qa), .QB(n74ls93_1_qb),
    .QC(n74ls93_1_qc), .QD(n74ls93_1_qd));
  _74LS92 u_74ls92_1 (
    .in_2(CLOCK_out), .in_3(1'b0), .in_4(1'b0), .out_6(n74ls92_1_out_6));  // open: in_1, out_5, out_7, out_8

  // Notes on the sheet:
  //   3.932160 MHz
  //   CLOCK
  //   Anyway, no need to draw all the 163s and all:
  //   Horizontal frequency = 3932160 / 256 = 15360 Hz
  //   Vertical frequency = 3932160 / 65536 = 60.0 Hz
  //   CLOCK/4
  //   OSI600 schematics pdf
  //   QD (CLOCK/8) to PHI0 ???
  //   SAM's Service Manual
  //   All other pins are unconnected
  //   CLOCK/8
  //   CLOCK/2
  //   983.040 kHz
  //   CLOCK/8
  //   CLOCK/3
  //   491.52 kHz
  //   1.966080 MHz
  //   491.52 kHz
  //   1.310720 MHz
  //   This looks WRONG
  //   I suspect it is just a LS93
  //   <---- this looks more like a ±1MHz clock for the 6502
  //   Even though the BOM says U29 is an LS92, too
endmodule
