// Logisim project OSI630.circ as structural Verilog: 1 circuit, main circuit main
module main (
  input  CD0,
  input  CD1,
  input  CD2,
  input  CD3,
  input  nCHLD,
  input  COLOR_EN,
  input  nBLANK,
  input  PIXELS,
  input  DB,
  input  nHS,
  input  nVS,
  output nCOMP_SYNC
);

  wire and_1_out, and_2_out, and_3_out, COMP__SYNC, n74ls175_1__1q, n74ls175_1__2_q, n74ls175_1__2q,
       n74ls175_1__3_q, n74ls175_1__3q, n74ls175_1__4_q, n74ls175_1__4q, nand_3_out, nand_4_out, nand_5_out,
       nand_6_out, nand_7_out, nand_8_out, nand_9_out, nand_10_out, nand_11_out, nand_12_out, nand_13_out,
       nand_14_out, nand_15_out, nSVID, VID1, xor_1_out, xor_4_out;

  xor xor_1 (xor_1_out, 1'b1, nCHLD);
  xor xor_2 (nCOMP_SYNC, 1'b1, COMP__SYNC);
  _74LS175 u_74ls175_1 (
    ._1D(CD0), ._2D(CD1), ._3D(CD2), ._4D(CD3), .CLOCK(xor_1_out), .nCLEAR(COLOR_EN), ._1Q(n74ls175_1__1q),
    ._2Q(n74ls175_1__2q), ._2_Q(n74ls175_1__2_q), ._3Q(n74ls175_1__3q), ._3_Q(n74ls175_1__3_q),
    ._4Q(n74ls175_1__4q), ._4_Q(n74ls175_1__4_q));  // open: _1_Q
  nand nand_1 (nSVID, VID1, DB);
  nand nand_2 (COMP__SYNC, nHS, nVS);
  xor xor_3 (VID1, PIXELS, n74ls175_1__1q);
  nand nand_3 (nand_3_out, nSVID, nSVID);
  nand nand_4 (nand_4_out, COMP__SYNC, COMP__SYNC);
  nand nand_5 (nand_5_out, n74ls175_1__2_q, n74ls175_1__3_q, n74ls175_1__4_q, xor_4_out);
  nand nand_6 (nand_6_out, n74ls175_1__2_q, n74ls175_1__3_q, n74ls175_1__4_q, nSVID);
  xor xor_4 (xor_4_out, 1'b1, nSVID);
  and and_1 (and_1_out, nand_6_out, nBLANK, n74ls175_1__2q);
  nand nand_7 (nand_7_out, n74ls175_1__2q, xor_4_out);
  and and_2 (and_2_out, nand_6_out, nBLANK, n74ls175_1__3q);
  nand nand_8 (nand_8_out, n74ls175_1__3q, xor_4_out);
  and and_3 (and_3_out, nand_6_out, nBLANK, n74ls175_1__4q);
  nand nand_9 (nand_9_out, n74ls175_1__4q, xor_4_out);
  LED led_1 (.in(nand_10_out));
  nand nand_10 (nand_10_out, and_1_out, nand_5_out);
  LED led_2 (.in(nand_11_out));
  nand nand_11 (nand_11_out, nand_7_out, nand_5_out);
  nand nand_12 (nand_12_out, and_2_out, nand_5_out);
  LED led_3 (.in(nand_12_out));
  LED led_4 (.in(nand_13_out));
  nand nand_13 (nand_13_out, nand_8_out, nand_5_out);
  LED led_5 (.in(nand_14_out));
  nand nand_14 (nand_14_out, and_3_out, nand_5_out);
  nand nand_15 (nand_15_out, nand_9_out, nand_5_out);
  LED led_6 (.in(nand_15_out));

  // Other names for the same wires on the sheet: VID = PIXELS

  // Notes on the sheet:
  //   (J3 pin 5)
  //   (seems unconnected
  //   on 600 side, set to 1)
  //   (set all three to 1)
  //   630
  //   600
  //   inverters disguised as XORs
  //   TO 630
  //   TO VIDEO COMP OUT AMP
  //   --------------------------------------------------------------------------------------------------------------------------------------------------------------------------------------------------------------------------------------------------------
  //   INVERT PIXEL!
  //   (if latched CD0 is 1)
  //   TO 630
  //   R OUT R-DIVIDER
  //   G OUT R-DIVIDER
  //   B OUT R-DIVIDER
  //   VIDEO OUT
  //   -----------------------------------------------
  //   NOTE THAT THIS IS
  //   INVERTED
  //   TTL RGB
  //   SIMILAR TO OLD NINTENDO
  //   ARCADE CGA
  //   -----------------------------------------------
endmodule
